# Fritzing sketch paul_line_follower (saved by Fritzing 0.9.2b)
circuit board: 8.46667cm x 5.64444cm
stripboards: 1

parts:
  3_3V_regulator_U1V11F3 = Pololu 3.3V Step-Up Voltage Regulator U1V11F3
  DRV8835_motor_driver = DRV8835 Dual Motor Driver Carrier
  Power_input_for_2×AAA_→ = male pin header, 2 pins [form="♂ (male)"]
  Pololu_Wixel = Wixel
  2x_sensors_from_QTR-8a = QTR-8x sensor - 2x sensors snapped off
  Part2 = Pololu 3.3V Step-Up Voltage Regulator U1V11F3
  Part1 = Pololu 3.3V Step-Up Voltage Regulator U1V11F3

nets (from the breadboard view):
  N1: 3_3V_regulator_U1V11F3.VIN, Power_input_for_2×AAA_→.pin1
  GND: 3_3V_regulator_U1V11F3.GND, DRV8835_motor_driver.VIN, DRV8835_motor_driver.GND, Power_input_for_2×AAA_→.pin2, Pololu_Wixel.GND, Pololu_Wixel.P0_3, 2x_sensors_from_QTR-8a.7, 2x_sensors_from_QTR-8a.GND#9
  VCC: 3_3V_regulator_U1V11F3.VOUT, DRV8835_motor_driver.VCC, DRV8835_motor_driver.MODE, Pololu_Wixel.VIN, 2x_sensors_from_QTR-8a.VCC
  N2: DRV8835_motor_driver.BIN2/BENABLE, DRV8835_motor_driver.AOUT1, Pololu_Wixel.P1_4, Part2.IN1
  N3: DRV8835_motor_driver.AIN2/AENABLE, Pololu_Wixel.P1_3
  N4: DRV8835_motor_driver.AOUT2, Part2.IN2
  N5: DRV8835_motor_driver.BOUT1, Part1.IN2
  N6: DRV8835_motor_driver.BOUT2, Part1.IN1
  N7: Pololu_Wixel.P0_4, 2x_sensors_from_QTR-8a.8
  N8: 2x_sensors_from_QTR-8a.GND#0, 2x_sensors_from_QTR-8a.2XR
